# Fritzing sketch Schematic (saved by Fritzing 0.9.4)
breadboards: 1

parts:
  Part1 = Arduino Uno (Rev3) - ICSP
  7_Segment1 = 7 Segment Display
  U1 = POT [package=pot_mammoth]
  RS485_module1 = RS485 Module (MAX3485)
  XLR1 = XLR NC3MAAH [package=nc3maah]  # not connected

nets:
  N1: Part1.A0, U1.A
  N2: Part1.D8, 7_Segment1.Segment_G
  N3: Part1.D9_PWM, 7_Segment1.Segment_DP
  N4: Part1.D12/MISO, RS485_module1.DI
  GND: Part1.GND, U1.E, RS485_module1.GND
  N5: Part1.D2, 7_Segment1.Segment_A
  N6: Part1.D3_PWM, 7_Segment1.Segment_B
  N7: Part1.D4, 7_Segment1.Segment_C
  N8: Part1.D5_PWM, 7_Segment1.Segment_D
  N9: Part1.D6_PWM, 7_Segment1.Segment_E
  N10: Part1.D7, 7_Segment1.Segment_F
  N11: Part1.5V, 7_Segment1.common_anode, U1.S
  N12: RS485_module1.VCC, RS485_module1.RE, RS485_module1.DE

custom parts:
  RS485 Module (MAX3485): Commercially available RS485 to RS232 TTL Module
